# Fritzing sketch RPM_TACHOMETER (saved by Fritzing 0.9.3b)
breadboards: 1

parts:
  U1 = NodeMCU V1.0  # not connected
  U2 = Sharp PC817 [package=THT]
  R1 = Resistor [tolerance=±5% resistance=470 package=THT]
  C1 = Ceramic Capacitor [capacitance=100nF voltage=35V package="100 mil [THT, multilayer]"]
  R2 = Resistor [tolerance=±5% resistance=220 package=THT]
  R4 = Resistor [tolerance=±5% resistance=470 package=THT]
  元件1 = TM1637
  R3 = Resistor [tolerance=±5% resistance=330 package=THT]
  D1 = Zener Diode [part_number=1N4732A breakdown_voltage=5.1V package="300 mil [THT]"]
  LED1 = smd LED [color="Red (633nm)" package="0603 [SMD]"]

nets:
  N1: U2.Pin_1, R2.Pin_1
  N2: U2.Pin_2, R1.Pin_0, C1.1, R4.Pin_1, 元件1.VCC, D1.anode
  N3: U2.Pin_4, R4.Pin_0, 元件1.GND, R3.Pin_1, D1.cathode
  N4: U2.Pin_3, C1.0
  N5: R2.Pin_0, LED1.anode

notes:
  Nodemcu V2
  VCC 12V
  470Ω
  鉭質電容0.1㎌ / 35V
  這顆不接應該也是可以
  GND
  接脈衝訊號(凸台)，或轉速訊號
  此排為 12V
  此排為 5V
  基納 5.1V
  PC817
  220Ω
  330Ω
  七段數位轉速表 TM1637
  CLK : D7
  DIO : D6
  轉速訊號 : 透過 PC817 接到 D1
  By 羽山秋人 (https://3wa.tw)
  LED

custom parts:
  NodeMCU V1.0: ESP8266 based NodeMCU V1.0
  TM1637: A 4 7-seg display
